// Logisim project Lab1.circ as structural Verilog: 1 circuit, main circuit main
module main (
  input  in_1,
  input  in_2,
  input  in_3,
  input  in_4,
  input  in_5,
  input  in_6,
  input  in_7,
  output out_8,
  output out_9,
  output out_10,
  output out_11,
  output out_12
);

  wire and_1_out, clock_1_out;

  Clock clock_1 (.out(clock_1_out));
  and and_1 (and_1_out, in_1, in_2);
  or or_1 (out_8, and_1_out, in_3);
  Register #(.width(4)) register_1 (
    .D({in_7, in_6, in_5, in_4}), .en(1'b1), .Q({out_12, out_11, out_10, out_9}), .clk(clock_1_out));  // open: clr

  // Notes on the sheet:
  //   3.1
  //   3.2
endmodule
