// Logisim project lab2.circ as structural Verilog: 1 circuit, main circuit main
module main (
  input  [7:0] in_1,
  input  [7:0] in_2,
  input  [2:0] in_3,
  input  [7:0] in_4,
  input  [1:0] in_5,
  input  in_6,
  output [7:0] out_7,
  output [7:0] out_8
);

  wire clock_1_out, decoder_1_out0, decoder_1_out1, decoder_1_out2, decoder_1_out3;
  wire [1:0] not_1_out;
  wire [7:0] adder_1_out, adder_2_out, and_1_out, nand_1_out, or_1_out, register_1_q, register_2_q,
       register_3_q, register_4_q, subtractor_1_out, subtractor_2_out, xor_1_out;

  Clock clock_1 (.out(clock_1_out));
  Decoder #(.select(2)) decoder_1 (
    .out0(decoder_1_out0), .out1(decoder_1_out1), .out2(decoder_1_out2), .out3(decoder_1_out3), .sel(in_5),
    .en(in_6));
  Subtractor subtractor_1 (.a(in_1), .b({8{1'b1}}), .out(subtractor_1_out));  // open: bin, bout
  Adder adder_1 (.a(in_1), .b({8{1'b1}}), .out(adder_1_out));  // open: cin, cout
  Adder adder_2 (.a(in_2), .b(in_1), .out(adder_2_out));  // open: cin, cout
  Subtractor subtractor_2 (.a(in_2), .b(in_1), .out(subtractor_2_out));  // open: bin, bout
  assign and_1_out = in_2 & in_1;  // AND_Gate and_1, 8 bits wide
  assign nand_1_out = ~(in_2 & in_1);  // NAND_Gate nand_1, 8 bits wide
  assign or_1_out = in_2 | in_1;  // OR_Gate or_1, 8 bits wide
  Register register_1 (.D(in_4), .en(decoder_1_out0), .Q(register_1_q), .clk(clock_1_out));  // open: clr
  Register register_2 (.D(in_4), .en(decoder_1_out1), .Q(register_2_q), .clk(clock_1_out));  // open: clr
  Register register_3 (.D(in_4), .en(decoder_1_out2), .Q(register_3_q), .clk(clock_1_out));  // open: clr
  Register register_4 (.D(in_4), .en(decoder_1_out3), .Q(register_4_q), .clk(clock_1_out));  // open: clr
  assign xor_1_out = in_2 ^ in_1;  // XOR_Gate xor_1, 8 bits wide
  assign not_1_out = ~in_5;  // NOT_Gate not_1, 2 bits wide
  Multiplexer #(.select(2), .width(8)) multiplexer_1 (
    .in0(register_1_q), .in1(register_2_q), .in2(register_3_q), .in3(register_4_q), .out(out_8),
    .sel(not_1_out));  // open: en
  Multiplexer #(.select(3), .width(8)) multiplexer_2 (
    .in0(subtractor_1_out), .in1(adder_1_out), .in2(adder_2_out), .in3(subtractor_2_out), .in4(and_1_out),
    .in5(nand_1_out), .in6(or_1_out), .in7(xor_1_out), .out(out_7), .sel(in_3));  // open: en
endmodule
